// Logisim project CPU.circ as structural Verilog: 1 circuit, main circuit main
module main (
  input  Clear
);

  wire alu_1_overflow, alu_1_zero, Beq_out, Bne_out, CLK_out, control_unit_v1_1_jump, EX_MEM_2_q, EX_MEM_3_q,
       EX_MEM_4_q, EX_MEM_6_q, EX_MEM_7_q, EX_MEM_10_q, EX_MEM_11_q, MEM_WB_2_q, MEM_WB_3_q, not_1_out;
  wire [2:0] EX_MEM_q, ID_EX_2_q, ID_EX_q, MEM_WB_q, multiplexer_1_out;
  wire [5:0] IF_ID_q_2, shifter_1_out;
  wire [9:0] IF_ID_q;
  wire [11:0] control_unit_v1_1_regdst, ID_EX_3_q;
  wire [15:0] adder_1_out, adder_2_out, alu_1_out_4, bit_extender_1_out, bit_extender_2_out, EX_MEM_5_q,
       EX_MEM_8_q, EX_MEM_9_q, ID_EX_4_q, ID_EX_5_q, ID_EX_6_q, ID_EX_7_q, ID_EX_8_q, IF_ID_2_q, MEM_WB_4_q,
       MEM_WB_5_q, multiplexer_2_out, multiplexer_3_out, multiplexer_4_out, multiplexer_5_out,
       multiplexer_6_out, PC_q, ram_1_data, register_file_1_data01, register_file_1_data02, rom_1_data,
       shifter_2_out;

  Clock CLK (.out(CLK_out));
  Register #(.width(16)) PC (.D(multiplexer_5_out), .Q(PC_q), .clk(CLK_out), .clr(Clear));  // open: en
  Adder #(.width(16)) adder_1 (.a(PC_q), .b(16'h1), .out(adder_1_out));  // open: cin, cout
  ROM #(.addrWidth(16), .dataWidth(16)) rom_1 (.addr(PC_q), .data(rom_1_data));  // open: sel
  Register #(.width(16)) IF_ID (.D(adder_1_out), .Q({IF_ID_q, IF_ID_q_2}), .clk(CLK_out));  // open: en, clr
  Register #(.width(16)) IF_ID_2 (.D(rom_1_data), .Q(IF_ID_2_q), .clk(CLK_out));  // open: en, clr
  Shifter #(.width(6)) shifter_1 (.in(IF_ID_2_q[5:0]), .\dist (3'b000), .out(shifter_1_out));
  Register #(.width(3)) ID_EX (.D(IF_ID_2_q[8:6]), .Q(ID_EX_q), .clk(CLK_out));  // open: en, clr
  Multiplexer #(.width(3)) multiplexer_1 (
    .in0(ID_EX_q), .in1(ID_EX_2_q), .out(multiplexer_1_out), .sel(ID_EX_3_q[0]));  // open: en
  Register #(.width(3)) ID_EX_2 (.D(IF_ID_2_q[5:3]), .Q(ID_EX_2_q), .clk(CLK_out));  // open: en, clr
  control_unit_v1 control_unit_v1_1 (
    .OPC1(IF_ID_2_q[15]), .RegDst(control_unit_v1_1_regdst[0]), .OPC2(IF_ID_2_q[14]), .OPC3(IF_ID_2_q[13]),
    .OPC4(IF_ID_2_q[12]), .ALUSrc1(control_unit_v1_1_regdst[1]), .ALUSrc2(control_unit_v1_1_regdst[2]),
    .MemToReg(control_unit_v1_1_regdst[3]), .RegWrite(control_unit_v1_1_regdst[4]),
    .MemRead(control_unit_v1_1_regdst[5]), .MemWrite(control_unit_v1_1_regdst[6]),
    .BranchBne(control_unit_v1_1_regdst[7]), .BranchBeq(control_unit_v1_1_regdst[8]),
    .ALUOP1(control_unit_v1_1_regdst[9]), .ALUOP2(control_unit_v1_1_regdst[10]),
    .ALUOP3(control_unit_v1_1_regdst[11]), .jump(control_unit_v1_1_jump));
  Register #(.width(3)) EX_MEM (.D(multiplexer_1_out), .Q(EX_MEM_q), .clk(CLK_out));  // open: en, clr
  assign bit_extender_1_out = {{13{IF_ID_2_q[2]}}, IF_ID_2_q[2:0]};  // Bit_Extender bit_extender_1
  assign bit_extender_2_out = {{10{IF_ID_2_q[5]}}, IF_ID_2_q[5:0]};  // Bit_Extender bit_extender_2
  Register #(.width(3)) MEM_WB (.D(EX_MEM_q), .Q(MEM_WB_q), .clk(CLK_out));  // open: en, clr
  Register #(.width(12)) ID_EX_3 (.D(control_unit_v1_1_regdst), .Q(ID_EX_3_q), .clk(CLK_out));  // open: en, clr
  Register_File register_file_1 (
    .Data_IN(multiplexer_6_out), .Data01(register_file_1_data01), .Data02(register_file_1_data02),
    .Data_Address(MEM_WB_q), .clk(CLK_out), .RS(IF_ID_2_q[11:9]), .RT(IF_ID_2_q[8:6]), .RegWrite(MEM_WB_2_q));
  Register #(.width(16)) ID_EX_4 (.D(bit_extender_1_out), .Q(ID_EX_4_q), .clk(CLK_out));  // open: en, clr
  Register #(.width(16)) ID_EX_5 (.D(bit_extender_2_out), .Q(ID_EX_5_q), .clk(CLK_out));  // open: en, clr
  Register #(.width(16)) ID_EX_6 (.D({IF_ID_q, IF_ID_q_2}), .Q(ID_EX_6_q), .clk(CLK_out));  // open: en, clr
  Register #(.width(16)) ID_EX_7 (.D(register_file_1_data01), .Q(ID_EX_7_q), .clk(CLK_out));  // open: en, clr
  Register #(.width(16)) ID_EX_8 (.D(register_file_1_data02), .Q(ID_EX_8_q), .clk(CLK_out));  // open: en, clr
  Multiplexer #(.select(2), .width(16)) multiplexer_2 (
    .in0(ID_EX_8_q), .in1(ID_EX_5_q), .in2(ID_EX_4_q), .out(multiplexer_2_out),
    .sel({ID_EX_3_q[1], ID_EX_3_q[2]}));  // open: in3, en
  Shifter #(.width(16)) shifter_2 (.in(ID_EX_5_q), .\dist (4'b0000), .out(shifter_2_out));
  Register #(.width(1)) MEM_WB_2 (.D(EX_MEM_2_q), .Q(MEM_WB_2_q), .clk(CLK_out));  // open: en, clr
  Register #(.width(1)) EX_MEM_2 (.D(ID_EX_3_q[4]), .Q(EX_MEM_2_q), .clk(CLK_out));  // open: en, clr
  Adder #(.width(16)) adder_2 (.a(ID_EX_6_q), .b(shifter_2_out), .out(adder_2_out));  // open: cin, cout
  Register #(.width(1)) EX_MEM_3 (.D(ID_EX_3_q[8]), .Q(EX_MEM_3_q), .clk(CLK_out));  // open: en, clr
  Register #(.width(1)) EX_MEM_4 (.D(ID_EX_3_q[7]), .Q(EX_MEM_4_q), .clk(CLK_out));  // open: en, clr
  ALU alu_1 (
    .A(ID_EX_7_q), .B(multiplexer_2_out), .out_4(alu_1_out_4),
    .Op({ID_EX_3_q[9], ID_EX_3_q[10], ID_EX_3_q[11]}), .Zero(alu_1_zero), .Overflow(alu_1_overflow));
  LED Overflow (.in(alu_1_overflow));
  Register #(.width(16)) EX_MEM_5 (.D(adder_2_out), .Q(EX_MEM_5_q), .clk(CLK_out));  // open: en, clr
  not not_1 (not_1_out, EX_MEM_6_q);
  Register #(.width(1)) EX_MEM_6 (.D(alu_1_zero), .Q(EX_MEM_6_q), .clk(CLK_out));  // open: en, clr
  Multiplexer #(.width(16)) multiplexer_3 (
    .in0(adder_1_out), .in1(EX_MEM_5_q), .out(multiplexer_3_out), .sel(Beq_out));  // open: en
  Register #(.width(1)) EX_MEM_7 (.D(ID_EX_3_q[5]), .Q(EX_MEM_7_q), .clk(CLK_out));  // open: en, clr
  and Beq (Beq_out, EX_MEM_3_q, EX_MEM_6_q);
  and Bne (Bne_out, EX_MEM_4_q, not_1_out);
  Register #(.width(16)) EX_MEM_8 (.D(alu_1_out_4), .Q(EX_MEM_8_q), .clk(CLK_out));  // open: en, clr
  Register #(.width(16)) EX_MEM_9 (.D(ID_EX_8_q), .Q(EX_MEM_9_q), .clk(CLK_out));  // open: en, clr
  Register #(.width(1)) EX_MEM_10 (.D(ID_EX_3_q[3]), .Q(EX_MEM_10_q), .clk(CLK_out));  // open: en, clr
  Register #(.width(1)) EX_MEM_11 (.D(ID_EX_3_q[6]), .Q(EX_MEM_11_q), .clk(CLK_out));  // open: en, clr
  Multiplexer #(.width(16)) multiplexer_4 (
    .in0(multiplexer_3_out), .in1(EX_MEM_5_q), .out(multiplexer_4_out), .sel(Bne_out));  // open: en
  Register #(.width(1)) MEM_WB_3 (.D(EX_MEM_10_q), .Q(MEM_WB_3_q), .clk(CLK_out));  // open: en, clr
  Multiplexer #(.width(16)) multiplexer_5 (
    .in0(multiplexer_4_out), .in1({IF_ID_q, shifter_1_out}), .out(multiplexer_5_out),
    .sel(control_unit_v1_1_jump));  // open: en
  RAM #(.addrWidth(16), .dataWidth(16), .bus("separate")) ram_1 (
    .addr(EX_MEM_8_q), .din(EX_MEM_9_q), .data(ram_1_data), .str(EX_MEM_11_q), .clk(CLK_out), .ld(EX_MEM_7_q));  // open: sel, clr
  Register #(.width(16)) MEM_WB_4 (.D(ram_1_data), .Q(MEM_WB_4_q), .clk(CLK_out));  // open: en, clr
  Register #(.width(16)) MEM_WB_5 (.D(EX_MEM_8_q), .Q(MEM_WB_5_q), .clk(CLK_out));  // open: en, clr
  Multiplexer #(.width(16)) multiplexer_6 (
    .in0(MEM_WB_5_q), .in1(MEM_WB_4_q), .out(multiplexer_6_out), .sel(MEM_WB_3_q));  // open: en

  // Notes on the sheet:
  //   Instruction
  //   contents of rom_1 (hex, n*v repeats v):
  //   a080 a0c2 1038 14e0
  //   JUMP - -OP[0-5]
  //   RD[3-5]
  //   OP[12-15]
  //   RS[9-11]
  //   RT[6-8]
  //   Shamt[0-2]
  //   IMM[0-5]
  //   RegDst
  //   RegWrite
  //   ALUSrc
  //   ALUOP
  //   MemWrite
  //   Jump
  //   Data Memory
  //   MemRead
  //   MemToReg
endmodule
