// Logisim project Register File(16 bit).circ as structural Verilog: 2 circuits, main circuit main
// CPU
module main (
);

  Register_File register_file_1 ();  // open: Data_IN, Data01, Data02, Data_Address, clk, RS, RT, RegWrite
endmodule

module Register_File (
  input  [15:0] Data_IN,
  input  RegWrite,
  input  [2:0] Data_Address,
  input  [2:0] RS,
  input  [2:0] RT,
  input  clk,
  output [15:0] Data01,
  output [15:0] Data02
);

  wire and_1_out, and_2_out, and_3_out, and_4_out, and_5_out, and_6_out, and_7_out, and_8_out,
       decoder_1_out0, decoder_1_out1, decoder_1_out2, decoder_1_out3, decoder_1_out4, decoder_1_out5,
       decoder_1_out6, decoder_1_out7;
  wire [15:0] register_1_q, register_2_q, register_3_q, register_4_q, register_5_q, register_6_q,
       register_7_q, register_8_q;

  Decoder #(.select(3)) decoder_1 (
    .out0(decoder_1_out0), .out1(decoder_1_out1), .out2(decoder_1_out2), .out3(decoder_1_out3),
    .out4(decoder_1_out4), .out5(decoder_1_out5), .out6(decoder_1_out6), .out7(decoder_1_out7),
    .sel(Data_Address));  // open: en
  and and_1 (and_1_out, decoder_1_out0, RegWrite);
  and and_2 (and_2_out, decoder_1_out1, RegWrite);
  and and_3 (and_3_out, decoder_1_out2, RegWrite);
  and and_4 (and_4_out, decoder_1_out3, RegWrite);
  and and_5 (and_5_out, decoder_1_out4, RegWrite);
  and and_6 (and_6_out, decoder_1_out5, RegWrite);
  and and_7 (and_7_out, decoder_1_out6, RegWrite);
  and and_8 (and_8_out, decoder_1_out7, RegWrite);
  Register #(.width(16)) register_1 (.D({16{1'b0}}), .en(and_1_out), .Q(register_1_q), .clk(clk));  // open: clr
  Register #(.width(16)) register_2 (.D(Data_IN), .en(and_2_out), .Q(register_2_q), .clk(clk));  // open: clr
  Register #(.width(16)) register_3 (.D(Data_IN), .en(and_3_out), .Q(register_3_q), .clk(clk));  // open: clr
  Register #(.width(16)) register_4 (.D(Data_IN), .en(and_4_out), .Q(register_4_q), .clk(clk));  // open: clr
  Register #(.width(16)) register_5 (.D(Data_IN), .en(and_5_out), .Q(register_5_q), .clk(clk));  // open: clr
  Register #(.width(16)) register_6 (.D(Data_IN), .en(and_6_out), .Q(register_6_q), .clk(clk));  // open: clr
  Register #(.width(16)) register_7 (.D(Data_IN), .en(and_7_out), .Q(register_7_q), .clk(clk));  // open: clr
  Register #(.width(16)) register_8 (.D(Data_IN), .en(and_8_out), .Q(register_8_q), .clk(clk));  // open: clr
  Multiplexer #(.select(3), .width(16)) multiplexer_1 (
    .in0(register_1_q), .in1(register_2_q), .in2(register_3_q), .in3(register_4_q), .in4(register_5_q),
    .in5(register_6_q), .in6(register_7_q), .in7(register_8_q), .out(Data01), .sel(RS));  // open: en
  Multiplexer #(.select(3), .width(16)) multiplexer_2 (
    .in0(register_1_q), .in1(register_2_q), .in2(register_3_q), .in3(register_4_q), .in4(register_5_q),
    .in5(register_6_q), .in6(register_7_q), .in7(register_8_q), .out(Data02), .sel(RT));  // open: en
endmodule
