// Logisim project update_ALU_16_BIT.circ as structural Verilog: 2 circuits, main circuit 16 bit ALU
module _16_bit_ALU (
  input  [15:0] A,
  input  [15:0] B,
  input  [2:0] OP,
  output ZERO,
  output [15:0] Result,
  output OVERFLOW
);

  wire not_2_out;
  wire [3:0] bit_extender_2_out;
  wire [15:0] adder_1_out, And_out, bit_extender_1_out, not_1_out, Or_out, overflow_1_output, shifter_1_out,
       shifter_2_out;

  assign bit_extender_1_out = {{15{1'b0}}, adder_1_out[15]};  // Bit_Extender bit_extender_1
  assign not_1_out = ~B;  // NOT_Gate not_1, 16 bits wide
  not not_2 (not_2_out, 1'b1);
  Bit_Extender #(.in_width(16), .out_width(4)) bit_extender_2 (.in(B), .out(bit_extender_2_out));
  assign And_out = A & B;  // AND_Gate And, 16 bits wide
  assign Or_out = A | B;  // OR_Gate Or, 16 bits wide
  Overflow overflow_1 (.A(A), .C_in(not_2_out), .B(B), .\output (overflow_1_output), .Overflow(OVERFLOW));
  Adder #(.width(16)) adder_1 (.a(A), .b(not_1_out), .out(adder_1_out), .cin(1'b1));  // open: cout
  Shifter #(.width(16)) shifter_1 (.in(A), .\dist (bit_extender_2_out), .out(shifter_1_out));
  Shifter #(.width(16), .shift("lr")) shifter_2 (.in(A), .\dist (bit_extender_2_out), .out(shifter_2_out));
  Multiplexer #(.select(3), .width(16)) multiplexer_1 (
    .in0(And_out), .in1(Or_out), .in2(overflow_1_output), .in3(adder_1_out), .in4(bit_extender_1_out),
    .in5(shifter_1_out), .in6(shifter_2_out), .out(Result), .sel(OP));  // open: in7, en
  nor nor_1 (ZERO, Result[0], Result[1], Result[2], Result[3], Result[4], Result[5], Result[6], Result[7], Result[9], Result[10], Result[10], Result[11], Result[12], Result[13], Result[14], Result[15]);

  // Notes on the sheet:
  //   Add
  //   sub
  //   Shift Left
  //   Shift Right
  //   SLT
endmodule

module ALU (
  input  [15:0] A,
  input  [15:0] B,
  input  [2:0] Op,
  output [15:0] out_4,
  output Zero,
  output Overflow
);

  _16_bit_ALU u_16_bit_alu_1 (.A(A), .B(B), .Result(out_4), .OP(Op), .ZERO(Zero), .OVERFLOW(Overflow));

  // Notes on the sheet:
  //   NAME
  //   AND
  //   OR
  //   ADD
  //   SUB
  //   LESS
  //   SHIFT LEFT
  //   SHIFT RIGHT
  //   OPERATION
  //   000
  //   001
  //   010
  //   011
  //   100
  //   101
  //   110
  //             SHIFT AMOUNT
  //   X
  //   X
  //   X
  //   X
  //   X
  //   0-7
  //   0-7
endmodule
