// Logisim project CPU.circ as structural Verilog: 1 circuit, main circuit main
module main (
  input  Clear,
  output [15:0] out_2
);

  wire alu_1_overflow, alu_1_zero, Beq_out, Bne_out, CLK_out, control_unit_v1_1_branchbeq,
       control_unit_v1_1_branchbne, control_unit_v1_1_jump, control_unit_v1_1_memread,
       control_unit_v1_1_memtoreg, control_unit_v1_1_memwrite, control_unit_v1_1_regdst,
       control_unit_v1_1_regwrite, not_1_out;
  wire [1:0] control_unit_v1_1_alusrc2;
  wire [2:0] control_unit_v1_1_aluop3, multiplexer_1_out;
  wire [5:0] shifter_1_out;
  wire [15:0] adder_1_out, adder_2_out, bit_extender_1_out, bit_extender_2_out, multiplexer_2_out,
       multiplexer_3_out, multiplexer_4_out, multiplexer_5_out, multiplexer_6_out, PC_q, ram_1_data,
       register_file_1_data01, register_file_1_data02, rom_1_data, shifter_2_out;

  Register #(.width(16)) PC (.D(multiplexer_5_out), .Q(PC_q), .clk(CLK_out), .clr(Clear));  // open: en
  Adder #(.width(16)) adder_1 (.a(PC_q), .b(16'h1), .out(adder_1_out));  // open: cin, cout
  ROM #(.addrWidth(16), .dataWidth(16)) rom_1 (.addr(PC_q), .data(rom_1_data));  // open: sel
  Shifter #(.width(6)) shifter_1 (.in(rom_1_data[5:0]), .\dist (3'b000), .out(shifter_1_out));
  control_unit_v1 control_unit_v1_1 (
    .OPC1(rom_1_data[15]), .RegDst(control_unit_v1_1_regdst), .OPC2(rom_1_data[14]), .OPC3(rom_1_data[13]),
    .OPC4(rom_1_data[12]), .ALUSrc1(control_unit_v1_1_alusrc2[1]), .ALUSrc2(control_unit_v1_1_alusrc2[0]),
    .MemToReg(control_unit_v1_1_memtoreg), .RegWrite(control_unit_v1_1_regwrite),
    .MemRead(control_unit_v1_1_memread), .MemWrite(control_unit_v1_1_memwrite),
    .BranchBne(control_unit_v1_1_branchbne), .BranchBeq(control_unit_v1_1_branchbeq),
    .ALUOP1(control_unit_v1_1_aluop3[2]), .ALUOP2(control_unit_v1_1_aluop3[1]),
    .ALUOP3(control_unit_v1_1_aluop3[0]), .jump(control_unit_v1_1_jump));
  Multiplexer #(.width(3)) multiplexer_1 (
    .in0(rom_1_data[8:6]), .in1(rom_1_data[5:3]), .out(multiplexer_1_out), .sel(control_unit_v1_1_regdst));  // open: en
  assign bit_extender_1_out = {{13{rom_1_data[2]}}, rom_1_data[2:0]};  // Bit_Extender bit_extender_1
  assign bit_extender_2_out = {{10{rom_1_data[5]}}, rom_1_data[5:0]};  // Bit_Extender bit_extender_2
  Register_File register_file_1 (
    .Data_IN(multiplexer_6_out), .Data01(register_file_1_data01), .Data02(register_file_1_data02),
    .Data_Address(multiplexer_1_out), .clk(CLK_out), .RS(rom_1_data[11:9]), .RT(rom_1_data[8:6]),
    .RegWrite(control_unit_v1_1_regwrite));
  Multiplexer #(.select(2), .width(16)) multiplexer_2 (
    .in0(register_file_1_data02), .in1(bit_extender_2_out), .in2(bit_extender_1_out),
    .out(multiplexer_2_out), .sel(control_unit_v1_1_alusrc2));  // open: in3, en
  Shifter #(.width(16)) shifter_2 (.in(bit_extender_2_out), .\dist (4'b0000), .out(shifter_2_out));
  Clock CLK (.out(CLK_out));
  Adder #(.width(16)) adder_2 (.a(adder_1_out), .b(shifter_2_out), .out(adder_2_out));  // open: cin, cout
  not not_1 (not_1_out, alu_1_zero);
  Multiplexer #(.width(16)) multiplexer_3 (
    .in0(adder_1_out), .in1(adder_2_out), .out(multiplexer_3_out), .sel(Beq_out));  // open: en
  and Beq (Beq_out, control_unit_v1_1_branchbeq, alu_1_zero);
  and Bne (Bne_out, control_unit_v1_1_branchbne, not_1_out);
  ALU alu_1 (
    .A(register_file_1_data01), .B(multiplexer_2_out), .out_4(out_2), .Op(control_unit_v1_1_aluop3),
    .Zero(alu_1_zero), .Overflow(alu_1_overflow));
  LED Overflow (.in(alu_1_overflow));
  Multiplexer #(.width(16)) multiplexer_4 (
    .in0(multiplexer_3_out), .in1(adder_2_out), .out(multiplexer_4_out), .sel(Bne_out));  // open: en
  Multiplexer #(.width(16)) multiplexer_5 (
    .in0(multiplexer_4_out), .in1({adder_1_out[15:6], shifter_1_out}), .out(multiplexer_5_out),
    .sel(control_unit_v1_1_jump));  // open: en
  RAM #(.addrWidth(16), .dataWidth(16), .bus("separate")) ram_1 (
    .addr(out_2), .din(register_file_1_data02), .data(ram_1_data), .str(control_unit_v1_1_memwrite),
    .clk(CLK_out), .ld(control_unit_v1_1_memread));  // open: sel, clr
  Multiplexer #(.width(16)) multiplexer_6 (
    .in0(out_2), .in1(ram_1_data), .out(multiplexer_6_out), .sel(control_unit_v1_1_memtoreg));  // open: en

  // Notes on the sheet:
  //   Instruction
  //   JUMP - -OP[0-5]
  //   contents of rom_1 (hex, n*v repeats v):
  //   a140 ab80 abc4 3dc8 4dd0 b044 b088 f007
  //   OP[12-15]
  //   RS[9-11]
  //   RT[6-8]
  //   RD[3-5]
  //   Shamt[0-2]
  //   IMM[0-5]
  //   RegDst
  //   RegWrite
  //   ALUSrc
  //   ALUOP
  //   MemWrite
  //   Jump
  //   Data Memory
  //   MemRead
  //   MemToReg
endmodule
