// Logisim project ControlUnit V2.circ as structural Verilog
module control_unit_v1 (
  input  OPC1,
  input  OPC2,
  input  OPC3,
  input  OPC4,
  output RegDst,
  output ALUSrc1,
  output ALUSrc2,
  output MemToReg,
  output RegWrite,
  output MemRead,
  output MemWrite,
  output BranchBne,
  output BranchBeq,
  output ALUOP1,
  output ALUOP2,
  output ALUOP3,
  output jump
);

  wire and_1_out, and_2_out, and_3_out, and_4_out, and_6_out, and_7_out, and_10_out, and_11_out, and_12_out,
       and_13_out, and_14_out, and_15_out, and_16_out, and_17_out, and_18_out, and_19_out, not_1_out,
       not_2_out, not_3_out, not_4_out, not_5_out, not_6_out, not_7_out, not_8_out, not_9_out, not_10_out,
       not_11_out, not_12_out, not_13_out, not_14_out, not_15_out, not_16_out, not_17_out, not_18_out,
       not_19_out, not_20_out, not_21_out, not_22_out, not_23_out, not_24_out, not_25_out, not_26_out,
       not_27_out, not_28_out, not_29_out, not_30_out, not_31_out, not_32_out;

  not not_1 (not_1_out, OPC1);
  not not_2 (not_2_out, OPC3);
  and and_1 (and_1_out, not_2_out, not_3_out);
  not not_3 (not_3_out, OPC4);
  and and_2 (and_2_out, OPC2, not_4_out);
  not not_4 (not_4_out, OPC3);
  not not_5 (not_5_out, OPC1);
  not not_6 (not_6_out, OPC3);
  not not_7 (not_7_out, OPC1);
  not not_8 (not_8_out, OPC4);
  and and_3 (and_3_out, OPC1, not_9_out);
  not not_9 (not_9_out, OPC2);
  and and_4 (and_4_out, OPC1, OPC3);
  and and_5 (MemToReg, OPC1, not_10_out);
  not not_10 (not_10_out, OPC4);
  not not_11 (not_11_out, OPC1);
  not not_12 (not_12_out, OPC2);
  and and_6 (and_6_out, not_12_out, not_13_out);
  not not_13 (not_13_out, OPC3);
  not not_14 (not_14_out, OPC2);
  and and_7 (and_7_out, not_14_out, not_15_out);
  not not_15 (not_15_out, OPC4);
  not not_16 (not_16_out, OPC2);
  and and_8 (MemRead, OPC1, not_16_out, not_17_out);
  not not_17 (not_17_out, OPC4);
  not not_18 (not_18_out, OPC2);
  not not_19 (not_19_out, OPC3);
  not not_20 (not_20_out, OPC3);
  and and_9 (BranchBeq, OPC1, not_20_out, not_21_out);
  not not_21 (not_21_out, OPC4);
  not not_22 (not_22_out, OPC1);
  and and_10 (and_10_out, not_22_out, OPC2, OPC4);
  not not_23 (not_23_out, OPC1);
  and and_11 (and_11_out, not_23_out, OPC2, OPC3);
  not not_24 (not_24_out, OPC2);
  and and_12 (and_12_out, not_24_out, not_25_out);
  not not_25 (not_25_out, OPC3);
  and and_13 (and_13_out, OPC3, not_26_out);
  not not_26 (not_26_out, OPC4);
  and and_14 (and_14_out, OPC1, not_27_out);
  not not_27 (not_27_out, OPC2);
  and and_15 (and_15_out, OPC1, not_28_out);
  not not_28 (not_28_out, OPC3);
  not not_29 (not_29_out, OPC1);
  not not_30 (not_30_out, OPC2);
  and and_16 (and_16_out, not_29_out, not_30_out, not_31_out);
  not not_31 (not_31_out, OPC4);
  and and_17 (and_17_out, OPC2, not_32_out);
  not not_32 (not_32_out, OPC3);
  or or_1 (RegDst, not_1_out, and_1_out, and_2_out);
  and and_18 (and_18_out, not_5_out, OPC2, not_6_out, OPC4);
  or or_2 (ALUSrc1, and_18_out, and_19_out);
  and and_19 (and_19_out, not_7_out, OPC2, OPC3, not_8_out);
  or or_3 (ALUSrc2, and_3_out, and_4_out);
  or or_4 (RegWrite, not_11_out, and_6_out, and_7_out);
  and and_20 (MemWrite, OPC1, not_18_out, OPC3, OPC4);
  and and_21 (BranchBne, OPC1, OPC2, not_19_out, OPC4);
  or or_5 (ALUOP1, and_10_out, and_11_out);
  or or_6 (ALUOP2, and_12_out, and_13_out, and_14_out, and_15_out);
  or or_7 (ALUOP3, and_16_out, and_17_out);
  and and_22 (jump, OPC4, OPC3, OPC2, OPC1);
endmodule

module test (
);

  control_unit_v1 control_unit_v1_1 ();  // open: OPC1, RegDst, OPC2, OPC3, OPC4, ALUSrc1, ALUSrc2, MemToReg, RegWrite, MemRead, MemWrite, BranchBne, BranchBeq, ALUOP1, ALUOP2, ALUOP3, jump
endmodule
