// Logisim project Overflow.circ as structural Verilog: 1 circuit, main circuit Overflow
module Overflow (
  input  [15:0] A,
  input  C_in,
  input  [15:0] B,
  output [15:0] \output ,
  output Overflow
);

  wire adder_1_cout, adder_2_cout, adder_3_cout, adder_4_cout, adder_5_cout, adder_6_cout, adder_7_cout,
       adder_8_cout, adder_9_cout, adder_10_cout, adder_11_cout, adder_12_cout, adder_13_cout, adder_14_cout,
       adder_15_cout, adder_16_cout;

  Adder #(.width(1)) adder_1 (.a(A[0]), .b(B[0]), .out(\output [0]), .cin(C_in), .cout(adder_1_cout));
  Adder #(.width(1)) adder_2 (.a(A[1]), .b(B[1]), .out(\output [1]), .cin(adder_1_cout), .cout(adder_2_cout));
  Adder #(.width(1)) adder_3 (.a(A[2]), .b(B[2]), .out(\output [2]), .cin(adder_2_cout), .cout(adder_3_cout));
  Adder #(.width(1)) adder_4 (.a(A[3]), .b(B[3]), .out(\output [3]), .cin(adder_3_cout), .cout(adder_4_cout));
  Adder #(.width(1)) adder_5 (.a(A[4]), .b(B[4]), .out(\output [4]), .cin(adder_4_cout), .cout(adder_5_cout));
  Adder #(.width(1)) adder_6 (.a(A[5]), .b(B[5]), .out(\output [5]), .cin(adder_5_cout), .cout(adder_6_cout));
  Adder #(.width(1)) adder_7 (.a(A[6]), .b(B[6]), .out(\output [6]), .cin(adder_6_cout), .cout(adder_7_cout));
  Adder #(.width(1)) adder_8 (.a(A[7]), .b(B[7]), .out(\output [7]), .cin(adder_7_cout), .cout(adder_8_cout));
  Adder #(.width(1)) adder_9 (.a(A[8]), .b(B[8]), .out(\output [8]), .cin(adder_8_cout), .cout(adder_9_cout));
  Adder #(.width(1)) adder_10 (.a(A[9]), .b(B[9]), .out(\output [9]), .cin(adder_9_cout), .cout(adder_10_cout));
  Adder #(.width(1)) adder_11 (.a(A[10]), .b(B[10]), .out(\output [10]), .cin(adder_10_cout), .cout(adder_11_cout));
  Adder #(.width(1)) adder_12 (.a(A[11]), .b(B[11]), .out(\output [11]), .cin(adder_11_cout), .cout(adder_12_cout));
  Adder #(.width(1)) adder_13 (.a(A[12]), .b(B[12]), .out(\output [12]), .cin(adder_12_cout), .cout(adder_13_cout));
  Adder #(.width(1)) adder_14 (.a(A[13]), .b(B[13]), .out(\output [13]), .cin(adder_13_cout), .cout(adder_14_cout));
  Adder #(.width(1)) adder_15 (.a(A[14]), .b(B[14]), .out(\output [14]), .cin(adder_14_cout), .cout(adder_15_cout));
  Adder #(.width(1)) adder_16 (.a(A[15]), .b(B[15]), .out(\output [15]), .cin(adder_15_cout), .cout(adder_16_cout));
  xor xor_1 (Overflow, adder_15_cout, adder_16_cout);
endmodule
