// Logisim project Datapath V2.circ as structural Verilog: 5 circuits, main circuit main
module main (
  input  [3:0] SLL,
  input  Cin,
  input  Clear,
  input  Immediate_select,
  input  Register_Write,
  input  ALU_source,
  input  [3:0] ALU_operation,
  input  Memory_Write,
  input  Memory_read,
  input  Result_select,
  input  Jump,
  input  Beq,
  output [9:0] Result,
  output [9:0] Data_1,
  output [9:0] Data_2,
  output [9:0] Instruction,
  output Zero,
  output [9:0] out_18,
  output Overflow,
  output [3:0] OP_code
);

  wire and_1_out, Clock_out;
  wire [1:0] multiplexer_1_out;
  wire [9:0] adder_1_out, adder_2_out, bit_extender_1_out, multiplexer_3_out, multiplexer_4_out, PC_q,
       ram_1_data, register_1_data_2, shifter_1_out;

  Clock Clock (.out(Clock_out));
  Register_part #(.width(10)) PC (.D(multiplexer_4_out), .Q(PC_q), .clk(Clock_out));  // open: en, clr
  Adder #(.width(10)) adder_1 (.a(10'h1), .b(PC_q), .out(adder_1_out));  // open: cin, cout
  ROM #(.addrWidth(10), .dataWidth(10)) rom_1 (.addr(PC_q), .data(Instruction));  // open: sel
  Multiplexer #(.width(2)) multiplexer_1 (
    .in0(Instruction[5:4]), .in1(Instruction[3:2]), .out(multiplexer_1_out), .sel(Immediate_select));  // open: en
  assign bit_extender_1_out = {{8{1'b0}}, Instruction[5:4]};  // Bit_Extender bit_extender_1
  Register register_1 (
    .RS(Instruction[1:0]), .Rt(Instruction[3:2]), .RD(multiplexer_1_out), .Write_data(out_18),
    .Clock(Clock_out), .RegWrite(Register_Write), .Data_1(Data_1), .Data_2(register_1_data_2));
  Multiplexer #(.width(10)) multiplexer_2 (
    .in0(register_1_data_2), .in1(bit_extender_1_out), .out(Data_2), .sel(ALU_source));  // open: en
  Shifter #(.width(10)) shifter_1 (.in(bit_extender_1_out), .\dist (SLL), .out(shifter_1_out));
  ALU_10__bit alu_10_bit_1 (
    .Cin(Cin), .A(Data_1), .B(Data_2), .Result(Result), .Overflow_detection(Overflow),
    .Operation(ALU_operation), .ZERO(Zero));
  Adder #(.width(10)) adder_2 (.a(adder_1_out), .b(shifter_1_out), .out(adder_2_out));  // open: cin, cout
  Multiplexer #(.width(10)) multiplexer_3 (
    .in0(adder_1_out), .in1(adder_2_out), .out(multiplexer_3_out), .sel(and_1_out));  // open: en
  and and_1 (and_1_out, Beq, Zero);
  Multiplexer #(.width(10)) multiplexer_4 (
    .in0(multiplexer_3_out), .in1(bit_extender_1_out), .out(multiplexer_4_out), .sel(Jump));  // open: en
  RAM #(.addrWidth(10), .dataWidth(10), .bus("separate")) ram_1 (
    .addr(Result), .din(register_1_data_2), .data(ram_1_data), .str(Memory_Write), .clk(Clock_out),
    .ld(Memory_read), .clr(Clear));  // open: sel
  Multiplexer #(.width(10)) multiplexer_5 (
    .in0(Result), .in1(ram_1_data), .out(out_18), .sel(Result_select));  // open: en

  assign OP_code = Instruction[9:6];

  // Notes on the sheet:
  //   Instruction memory
  //   contents of rom_1 (hex, n*v repeats v):
  //   2b1 12d 2b1 335 146 256 252 23 2b1 12d 2b1 335 146 256 252 23 123 231 321 54 245 254 223 21a 221 123
  //   231 321 54 245 254 223 21a 221 321 54 245 254 223 21a 221 123 231 321 54 245 254 223 21a 221
  //   Data memory
endmodule

// 1 bit
module ALU_1bit (
  input  Cin,
  input  A,
  input  B,
  input  [3:0] in_4,
  output Result,
  output Cout
);

  wire adder_1_out, comparator_1_eq, comparator_1_lt, multiplexer_1_out, nor_1_out, not_1_out, xor_1_out;

  not not_1 (not_1_out, B);
  xor xor_1 (xor_1_out, A, B);
  nor nor_1 (nor_1_out, A, B);
  Multiplexer multiplexer_1 (.in0(B), .in1(not_1_out), .out(multiplexer_1_out), .sel(in_4[3]));  // open: en
  Comparator #(.width(1), .mode("unsigned")) comparator_1 (
    .a(A), .b(B), .eq(comparator_1_eq), .lt(comparator_1_lt));  // open: gt
  Adder #(.width(1)) adder_1 (.a(A), .b(multiplexer_1_out), .out(adder_1_out), .cin(Cin), .cout(Cout));
  Multiplexer #(.select(3)) multiplexer_2 (
    .in0(xor_1_out), .in1(nor_1_out), .in2(adder_1_out), .in3(comparator_1_lt), .in4(comparator_1_eq),
    .out(Result), .sel(in_4[2:0]));  // open: in5, in6, in7, en

  // Notes on the sheet:
  //   B invert
  //   Operation
endmodule

// ALU
module ALU_10__bit (
  input  Cin,
  input  [9:0] A,
  input  [9:0] B,
  input  [3:0] Operation,
  output [9:0] Result,
  output ZERO,
  output Overflow_detection
);

  wire alu_1bit_1_cout, alu_1bit_2_cout, alu_1bit_3_cout, alu_1bit_4_cout, alu_1bit_5_cout, alu_1bit_6_cout,
       alu_1bit_7_cout, alu_1bit_8_cout, alu_1bit_9_cout, alu_1bit_10_cout;

  ALU_1bit alu_1bit_1 (.Cin(Cin), .A(A[0]), .B(B[0]), .Result(Result[0]), .Cout(alu_1bit_1_cout), .in_4(Operation));
  ALU_1bit alu_1bit_2 (
    .Cin(alu_1bit_1_cout), .A(A[1]), .B(B[1]), .Result(Result[1]), .Cout(alu_1bit_2_cout), .in_4(Operation));
  ALU_1bit alu_1bit_3 (
    .Cin(alu_1bit_2_cout), .A(A[2]), .B(B[2]), .Result(Result[2]), .Cout(alu_1bit_3_cout), .in_4(Operation));
  ALU_1bit alu_1bit_4 (
    .Cin(alu_1bit_3_cout), .A(A[3]), .B(B[3]), .Result(Result[3]), .Cout(alu_1bit_4_cout), .in_4(Operation));
  ALU_1bit alu_1bit_5 (
    .Cin(alu_1bit_4_cout), .A(A[4]), .B(B[4]), .Result(Result[4]), .Cout(alu_1bit_5_cout), .in_4(Operation));
  ALU_1bit alu_1bit_6 (
    .Cin(alu_1bit_5_cout), .A(A[5]), .B(B[5]), .Result(Result[5]), .Cout(alu_1bit_6_cout), .in_4(Operation));
  ALU_1bit alu_1bit_7 (
    .Cin(alu_1bit_6_cout), .A(A[6]), .B(B[6]), .Result(Result[6]), .Cout(alu_1bit_7_cout), .in_4(Operation));
  ALU_1bit alu_1bit_8 (
    .Cin(alu_1bit_7_cout), .A(A[7]), .B(B[7]), .Result(Result[7]), .Cout(alu_1bit_8_cout), .in_4(Operation));
  ALU_1bit alu_1bit_9 (
    .Cin(alu_1bit_8_cout), .A(A[8]), .B(B[8]), .Result(Result[8]), .Cout(alu_1bit_9_cout), .in_4(Operation));
  ALU_1bit alu_1bit_10 (
    .Cin(alu_1bit_9_cout), .A(A[9]), .B(B[9]), .Result(Result[9]), .Cout(alu_1bit_10_cout), .in_4(Operation));
  and and_1 (ZERO, Result[0], Result[1], Result[2], Result[4], Result[5], Result[6], Result[7], Result[8], Result[9], Result[3]);
  xor xor_1 (Overflow_detection, alu_1bit_9_cout, alu_1bit_10_cout);
endmodule

module Register_file (
  input  [9:0] Data_IN,
  input  Reg_Write,
  input  [1:0] Data_Address,
  input  [1:0] RS,
  input  clk,
  input  [1:0] RT,
  output [9:0] Data01,
  output [9:0] Data02
);

  wire and_1_out, and_2_out, and_3_out, and_4_out, decoder_1_out0, decoder_1_out1, decoder_1_out2,
       decoder_1_out3;
  wire [9:0] register_1_q, register_2_q, register_3_q, register_4_q;

  Decoder #(.select(2)) decoder_1 (
    .out0(decoder_1_out0), .out1(decoder_1_out1), .out2(decoder_1_out2), .out3(decoder_1_out3),
    .sel(Data_Address));  // open: en
  and and_1 (and_1_out, Reg_Write, decoder_1_out0);
  and and_2 (and_2_out, Reg_Write, decoder_1_out1);
  and and_3 (and_3_out, Reg_Write, decoder_1_out2);
  and and_4 (and_4_out, Reg_Write, decoder_1_out3);
  Register_part #(.width(10)) register_1 (.D(Data_IN), .en(and_1_out), .Q(register_1_q), .clk(clk));  // open: clr
  Register_part #(.width(10)) register_2 (.D(Data_IN), .en(and_2_out), .Q(register_2_q), .clk(clk));  // open: clr
  Register_part #(.width(10)) register_3 (.D(Data_IN), .en(and_3_out), .Q(register_3_q), .clk(clk));  // open: clr
  Register_part #(.width(10)) register_4 (.D(Data_IN), .en(and_4_out), .Q(register_4_q), .clk(clk));  // open: clr
  Multiplexer #(.select(2), .width(10)) multiplexer_1 (
    .in0(register_1_q), .in1(register_2_q), .in2(register_3_q), .in3(register_4_q), .out(Data01), .sel(RS));  // open: en
  Multiplexer #(.select(2), .width(10)) multiplexer_2 (
    .in0(register_1_q), .in1(register_2_q), .in2(register_3_q), .in3(register_4_q), .out(Data02), .sel(RT));  // open: en
endmodule

module Register (
  input  [1:0] RS,
  input  [1:0] Rt,
  input  [1:0] RD,
  input  [9:0] Write_data,
  input  Clock,
  input  RegWrite,
  output [9:0] Data_1,
  output [9:0] Data_2
);

  Register_file Register_file (
    .Data_IN(Write_data), .Data01(Data_1), .Data02(Data_2), .Data_Address(RD), .clk(Clock), .RS(RS), .RT(Rt),
    .Reg_Write(RegWrite));
endmodule
